# Fritzing sketch velostat (saved by Fritzing 0.9.2b)
breadboards: 1

parts:
  パーツ1 = Arduino Uno (Rev3)
  R1 = Resistor [tolerance=±5% resistance=1k package=THT]
  LED1 = LED - 5mm [color="Red (633nm)" package="5 mm [THT]"]
  R2 = Textile Analog Pressure Sensor [part_number=PW073]  # not connected

nets:
  N1: パーツ1.A0, R1.Pin_1
  N2: パーツ1.GND, LED1.cathode
  N3: パーツ1.D6_PWM, LED1.anode
  N4: パーツ1.3V3, R1.Pin_0
